# Fritzing sketch project-setup (saved by Fritzing 0.9.3b)

parts:
  Arduino_Pro_Mini_3_3V_8_Mhz = Arduino Pro Mini v13
  Arduino_Uno = Arduino Uno (Rev3)
  1-RFM69W = RFM69W HopeRF RF 13dBm RF transceiver
  2-RFM69W = RFM69W HopeRF RF 13dBm RF transceiver

nets:
  VCC: Arduino_Pro_Mini_3_3V_8_Mhz.VCC, 2-RFM69W.3.3V
  GND: Arduino_Pro_Mini_3_3V_8_Mhz.GND, 2-RFM69W.GND
  N1: Arduino_Pro_Mini_3_3V_8_Mhz.D13/SCK, 2-RFM69W.SCK
  N2: Arduino_Pro_Mini_3_3V_8_Mhz.D12/MISO, 2-RFM69W.MISO
  N3: Arduino_Pro_Mini_3_3V_8_Mhz.D11_PWM/MOSI, 2-RFM69W.MOSI
  N4: Arduino_Pro_Mini_3_3V_8_Mhz.D10_PWM/SS, 2-RFM69W.NSS
  N5: Arduino_Pro_Mini_3_3V_8_Mhz.D9_PWM, 2-RFM69W.RESET
  N6: Arduino_Pro_Mini_3_3V_8_Mhz.D2, 2-RFM69W.DIO0
  N7: Arduino_Uno.D10_PWM/SS, 1-RFM69W.NSS
  N8: Arduino_Uno.D11_PWM/MOSI, 1-RFM69W.MOSI
  N9: Arduino_Uno.D12/MISO, 1-RFM69W.MISO
  N10: Arduino_Uno.D13/SCK, 1-RFM69W.SCK
  GND_2: Arduino_Uno.GND, 1-RFM69W.GND
  N11: Arduino_Uno.D2, 1-RFM69W.DIO0
  3V3: Arduino_Uno.3V3, 1-RFM69W.3.3V

custom parts:
  RFM69W HopeRF RF 13dBm RF transceiver: The RFM69W is a highly integrated RF transceiver capable of operation over a wide frequency range, including the 433, 868 and 915 MHz license-free ISM (Industry Scientific and Medical) frequency bands. Its highly integrated architecture allows for a minimum of external components whilst maintaining maximum design flexibility. All major RF communication parameters are programmable and most of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

// code stored in the sketch: Receiver.ino
/* RFM69 library and code by Felix Rusu - felix@lowpowerlab.com
// Get libraries at: https://github.com/LowPowerLab/
// Make sure you adjust the settings in the configuration section below !!!
// **********************************************************************************
// Copyright Felix Rusu, LowPowerLab.com
// Library and code by Felix Rusu - felix@lowpowerlab.com
// **********************************************************************************
// License
// **********************************************************************************
// This program is free software; you can redistribute it 
// and/or modify it under the terms of the GNU General    
// Public License as published by the Free Software       
// Foundation; either version 3 of the License, or        
// (at your option) any later version.                    
//                                                        
// This program is distributed in the hope that it will   
// be useful, but WITHOUT ANY WARRANTY; without even the  
// implied warranty of MERCHANTABILITY or FITNESS FOR A   
// PARTICULAR PURPOSE. See the GNU General Public        
// License for more details.                              
//                                                        
// You should have received a copy of the GNU General    
// Public License along with this program.
// If not, see <http://www.gnu.org/licenses></http:>.
//                                                        
// Licence can be viewed at                               
// http://www.gnu.org/licenses/gpl-3.0.txt
//
// Please maintain this license information along with authorship
// and copyright notices in any redistribution of this code
// **********************************************************************************/

#include <RFM69.h>    //get it here: https://www.github.com/lowpowerlab/rfm69
#include <SPI.h>

//*********************************************************************************************
// *********** IMPORTANT SETTINGS - YOU MUST CHANGE/ONFIGURE TO FIT YOUR HARDWARE *************
//*********************************************************************************************
#define NETWORKID     100  //the same on all nodes that talk to each other
#define NODEID        1  

//Match frequency to the hardware version of the radio
#define FREQUENCY     RF69_433MHZ
//#define FREQUENCY     RF69_868MHZ
//#define FREQUENCY      RF69_915MHZ
#define ENCRYPTKEY     "sampleEncryptKey" //exactly the same 16 characters/bytes on all nodes!
#define IS_RFM69HCW    false // set to 'true' if you are using an RFM69HCW module

//*********************************************************************************************
#define SERIAL_BAUD   115200

#define RFM69_CS      10
#define RFM69_IRQ     2
#define RFM69_IRQN    0  // Pin 2 is IRQ 0!
#define RFM69_RST     9

#define LED           8  // onboard blinky

int16_t packetnum = 0;  // packet counter, we increment per xmission

RFM69 radio = RFM69(RFM69_CS, RFM69_IRQ, IS_RFM69HCW, RFM69_IRQN);

void setup() {
//  while (!Serial); // wait until serial console is open, remove if not tethered to computer
  Serial.begin(SERIAL_BAUD);

  Serial.println("RFM69W Receiver");
  
  // Hard Reset the RFM module
  pinMode(RFM69_RST, OUTPUT);
  digitalWrite(RFM69_RST, HIGH);
  delay(100);
  digitalWrite(RFM69_RST, LOW);
  delay(100);
  
  // Initialize radio
  radio.initialize(FREQUENCY,NODEID,NETWORKID);
  if (IS_RFM69HCW) {
    radio.setHighPower();    // Only for RFM69HCW & HW!
  }
  radio.setPowerLevel(31); // power output ranges from 0 (5dBm) to 31 (20dBm)
  
  radio.encrypt(ENCRYPTKEY);
  
  pinMode(LED, OUTPUT);

  Serial.print("\nListening at ");
  Serial.print(FREQUENCY==RF69_433MHZ ? 433 : FREQUENCY==RF69_868MHZ ? 868 : 915);
  Serial.println(" MHz");
}

void loop() {
  //check if something was received (could be an interrupt from the radio)
  if (radio.receiveDone())
  {
    //print message received to serial
    Serial.print('[');Serial.print(radio.SENDERID);Serial.print("] ");
    Serial.print((char*)radio.DATA);
    Serial.print("   [RX_RSSI:");Serial.print(radio.RSSI);Serial.print("]");

    //check if received message contains Hello World
    if (strstr((char *)radio.DATA, "Hello World"))
    {
      //check if sender wanted an ACK
      if (radio.ACKRequested())
      {
        radio.sendACK();
        Serial.println(" - ACK sent");
      }
      Blink(LED, 40, 3); //blink LED 3 times, 40ms between blinks
    }  
  }

  radio.receiveDone(); //put radio in RX mode
  Serial.flush(); //make sure all serial data is clocked out before sleeping the MCU
}

void Blink(byte PIN, byte DELAY_MS, byte loops)
{
  for (byte i=0; i<loops; i++)
  {
    digitalWrite(PIN,HIGH);
    delay(DELAY_MS);
    digitalWrite(PIN,LOW);
    delay(DELAY_MS);
  }
}

// code stored in the sketch: Transmitter.ino
    /* RFM69 library and code by Felix Rusu - felix@lowpowerlab.com
    // Get libraries at: https://github.com/LowPowerLab/
    // Make sure you adjust the settings in the configuration section below !!!
    // **********************************************************************************
    // Copyright Felix Rusu, LowPowerLab.com
    // Library and code by Felix Rusu - felix@lowpowerlab.com
    // **********************************************************************************
    // License
    // **********************************************************************************
    // This program is free software; you can redistribute it 
    // and/or modify it under the terms of the GNU General    
    // Public License as published by the Free Software       
    // Foundation; either version 3 of the License, or        
    // (at your option) any later version.                    
    //                                                        
    // This program is distributed in the hope that it will   
    // be useful, but WITHOUT ANY WARRANTY; without even the  
    // implied warranty of MERCHANTABILITY or FITNESS FOR A   
    // PARTICULAR PURPOSE. See the GNU General Public        
    // License for more details.                              
    //                                                        
    // You should have received a copy of the GNU General    
    // Public License along with this program.
    // If not, see <http://www.gnu.org/licenses></http:>.
    //                                                        
    // Licence can be viewed at                               
    // http://www.gnu.org/licenses/gpl-3.0.txt
    //
    // Please maintain this license information along with authorship
    // and copyright notices in any redistribution of this code
    // **********************************************************************************/
     
    #include <RFM69.h>    //get it here: https://www.github.com/lowpowerlab/rfm69
    #include <SPI.h>
     
    //*********************************************************************************************
    // *********** IMPORTANT SETTINGS - YOU MUST CHANGE/ONFIGURE TO FIT YOUR HARDWARE *************
    //*********************************************************************************************
    #define NETWORKID     100  // The same on all nodes that talk to each other
    #define NODEID        2    // The unique identifier of this node
    #define RECEIVER      1    // The recipient of packets
     
    //Match frequency to the hardware version of the radio on your Feather
    #define FREQUENCY     RF69_433MHZ
    //#define FREQUENCY     RF69_868MHZ
    //#define FREQUENCY     RF69_915MHZ
    #define ENCRYPTKEY    "sampleEncryptKey" //exactly the same 16 characters/bytes on all nodes!
    #define IS_RFM69HCW   false // set to 'true' if you are using an RFM69HCW module
     
    //*********************************************************************************************
    #define SERIAL_BAUD   115200
     
    #define RFM69_CS      10
    #define RFM69_IRQ     2
    #define RFM69_IRQN    0  // Pin 2 is IRQ 0!
    #define RFM69_RST     9
     
    #define LED           8  // onboard blinky
     
     
    int16_t packetnum = 0;  // packet counter, we increment per xmission
     
    RFM69 radio = RFM69(RFM69_CS, RFM69_IRQ, IS_RFM69HCW, RFM69_IRQN);
     
    void setup() {
      while (!Serial); // wait until serial console is open, remove if not tethered to computer
      Serial.begin(SERIAL_BAUD);
     
      Serial.println("Arduino RFM69W Transmitter");
      
      // Hard Reset the RFM module
      pinMode(RFM69_RST, OUTPUT);
      digitalWrite(RFM69_RST, HIGH);
      delay(100);
      digitalWrite(RFM69_RST, LOW);
      delay(100);
     
      // Initialize radio
      radio.initialize(FREQUENCY,NODEID,NETWORKID);
      if (IS_RFM69HCW) {
        radio.setHighPower();    // Only for RFM69HCW & HW!
      }
      radio.setPowerLevel(31); // power output ranges from 0 (5dBm) to 31 (20dBm)
      
      radio.encrypt(ENCRYPTKEY);
      
      pinMode(LED, OUTPUT);
      Serial.print("\nTransmitting at ");
      Serial.print(FREQUENCY==RF69_433MHZ ? 433 : FREQUENCY==RF69_868MHZ ? 868 : 915);
      Serial.println(" MHz");
    }
     
     
    void loop() {
      delay(1000);  // Wait 1 second between transmits, could also 'sleep' here!
        
      char radiopacket[20] = "Hello World #";
      itoa(packetnum++, radiopacket+13, 10);
      Serial.print("Sending "); Serial.println(radiopacket);
        
      if (radio.sendWithRetry(RECEIVER, radiopacket, strlen(radiopacket))) { //target node Id, message as string or byte array, message length
        Serial.println("OK");
        Blink(LED, 50, 3); //blink LED 3 times, 50ms between blinks
      }
     
      radio.receiveDone(); //put radio in RX mode
      Serial.flush(); //make sure all serial data is clocked out before sleeping the MCU
    }
     
    void Blink(byte PIN, byte DELAY_MS, byte loops)
    {
      for (byte i=0; i<loops; i++)
      {
        digitalWrite(PIN,HIGH);
        delay(DELAY_MS);
        digitalWrite(PIN,LOW);
        delay(DELAY_MS);
      }
    }
